# Fritzing sketch D12_V2 (saved by Fritzing 0.9.3b)
circuit board: 9.73cm x 9.2553cm
breadboards: 1

parts:
  U1 = ESP8266 WiFi Module [part_number=ESP8266]
  R1 = Resistor [tolerance=±5% resistance=220 package=THT]
  R2 = Resistor [tolerance=±5% resistance=220 package=THT]
  R3 = Resistor [tolerance=±5% resistance=220 package=THT]
  R4 = Resistor [tolerance=±5% resistance=220 package=THT]
  R5 = Resistor [tolerance=±5% resistance=220 package=THT]
  R6 = Resistor [tolerance=±5% resistance=220 package=THT]
  LED1 = LED - 5mm [color="Red (633nm)" package="5 mm [THT]"]
  LED2 = LED - 5mm [color="Red (633nm)" package="5 mm [THT]"]
  J1 = female pin header, 5 pins [form="♀ (female)"]
  J2 = female pin header, 5 pins [form="♀ (female)"]
  S1 = Pushbutton [package="[THT]"]
  J4 = female pin header, 2 pins [form="♀ (female)"]
  R7 = Resistor [tolerance=±5% resistance=220 package=THT]
  R8 = Resistor [tolerance=±5% resistance=220 package=THT]
  R9 = Resistor [tolerance=±5% resistance=220 package=THT]
  R10 = Resistor [tolerance=±5% resistance=220 package=THT]
  R11 = Resistor [tolerance=±5% resistance=220 package=THT]
  R12 = Resistor [tolerance=±5% resistance=220 package=THT]
  LED3 = LED - 5mm [color="Red (633nm)" package="5 mm [THT]"]
  LED4 = LED - 5mm [color="Red (633nm)" package="5 mm [THT]"]
  J5 = female pin header, 5 pins [form="♀ (female)"]
  J6 = female pin header, 5 pins [form="♀ (female)"]
  S2 = Pushbutton [package="[THT]"]
  J8 = female pin header, 2 pins [form="♀ (female)"]
  U2 = ESP8266 WiFi Module [part_number=ESP8266]
  J9 = female pin header, 2 pins [form="♀ (female)"]
  J10 = female pin header, 2 pins [form="♀ (female)"]
  J7 = female pin header, 6 pins [form="♀ (female)"]
  J3 = female pin header, 6 pins [form="♀ (female)"]
  R13 = Resistor [tolerance=±5% resistance=220 package=THT]
  R14 = Resistor [tolerance=±5% resistance=220 package=THT]
  R15 = Resistor [tolerance=±5% resistance=220 package=THT]
  R16 = Resistor [tolerance=±5% resistance=220 package=THT]
  R23 = Resistor [tolerance=±5% resistance=220 package=THT]
  R24 = Resistor [tolerance=±5% resistance=220 package=THT]
  R25 = Resistor [tolerance=±5% resistance=220 package=THT]
  R26 = Resistor [tolerance=±5% resistance=220 package=THT]
  R27 = Resistor [tolerance=±5% resistance=220 package=THT]
  R28 = Resistor [tolerance=±5% resistance=220 package=THT]
  J11 = double row female pin header, 4 pins [form="♀ (female)"]

nets:
  N1: U1.RXD, J9.pin2, J3.pin2
  N2: U1.VCC, R1.Pin_0, R2.Pin_0, R3.Pin_0, J4.pin2, J3.pin4, R23.Pin_1, R24.Pin_1, R25.Pin_1, R26.Pin_1, R27.Pin_1, J11.pin1
  N3: U1.GPIO_0, R1.Pin_1, J3.pin5
  N4: U1.GPIO_2, J1.pin1, R25.Pin_0
  N5: U1.CH_PD, R3.Pin_1
  N6: U1.GND, R4.Pin_0, LED1.anode, LED2.anode, J2.pin1, J2.pin2, J2.pin3, J2.pin4, J2.pin5, S1.Pin_1, S1.Pin_2, J4.pin1, J3.pin3, J3.pin6, J11.pin2
  N7: U1.TXD, J10.pin2, J3.pin1
  N8: U1.GPIO_15, R4.Pin_1
  N9: U1.GPIO_4, R6.Pin_0
  N10: U1.GPIO_5, R5.Pin_1
  N11: U1.GPIO_16, J1.pin5, R24.Pin_0
  N12: U1.GPIO_14, J1.pin4, R23.Pin_0
  N13: U1.GPIO_12, J1.pin3, R26.Pin_0
  N14: U1.GPIO_13, J1.pin2, R27.Pin_0
  N15: U1.REST, R2.Pin_1, S1.Pin_3, S1.Pin_4
  N16: R5.Pin_0, LED2.cathode
  N17: R6.Pin_1, LED1.cathode
  N18: R7.Pin_0, U2.GPIO_4
  N19: R7.Pin_1, LED4.cathode
  N20: R8.Pin_0, LED3.cathode
  N21: R8.Pin_1, U2.GPIO_5
  N22: R9.Pin_0, LED3.anode, LED4.anode, J5.pin1, J5.pin2, J5.pin3, J5.pin4, J5.pin5, S2.Pin_1, S2.Pin_2, J8.pin2, U2.GND, J7.pin3, J7.pin6, J11.pin3
  N23: R9.Pin_1, U2.GPIO_15
  N24: R10.Pin_0, R11.Pin_0, R12.Pin_0, J8.pin1, U2.VCC, J7.pin4, R13.Pin_1, R14.Pin_1, R15.Pin_1, R16.Pin_1, R28.Pin_1, J11.pin4
  N25: R10.Pin_1, U2.CH_PD
  N26: R11.Pin_1, S2.Pin_3, S2.Pin_4, U2.REST
  N27: R12.Pin_1, U2.GPIO_0, J7.pin5
  N28: J6.pin1, U2.GPIO_2, R28.Pin_0
  N29: J6.pin2, U2.GPIO_13, R16.Pin_0
  N30: J6.pin3, U2.GPIO_12, R13.Pin_0
  N31: J6.pin4, U2.GPIO_14, R14.Pin_0
  N32: J6.pin5, U2.GPIO_16, R15.Pin_0
  N33: U2.RXD, J10.pin1, J7.pin2
  N34: U2.TXD, J9.pin1, J7.pin1

notes:
  R1
  R2
  R3
  R4
  R5
  R6
  VIN
  VOUT
  GND
  1
  2
  4
  8
  M
  RX
  TX
  3v3
  JMP
  PRGM
  COMM
  RST
  LIVE
  github.com/GlitchOne
  Dodecauthenticator V1.7
  1 0f 11
  SMA
  2.2mm
  Glitch1 2019
